# Fritzing sketch Esquematico_Receptor_nrf24l01 (saved by Fritzing 0.9.2b)
breadboards: 1

parts:
  Parte1 = Arduino Mega ADK (Rev3)
  U1 = LCD-16X2 [package=lcd-16x2]
  R35 = Rotary Potentiometer (Large) [maximum_resistance=10kΩ package=THT]
  Componente2 = nRF24L01+

nets:
  3V3: Parte1.3V3, Componente2.VCC
  5V: Parte1.5V, U1.VDD, U1.A, R35.leg2
  GND: Parte1.GND, U1.VSS, U1.K, R35.leg1, Componente2.GND
  N1: Parte1.D22, U1.DB7
  N2: Parte1.D24, U1.DB6
  N3: Parte1.D26, U1.DB5
  N4: Parte1.D28, U1.DB4
  N5: Parte1.D30, U1.E
  N6: Parte1.D32, U1.R_W
  N7: Parte1.D34, U1.RS
  N8: Parte1.D48, Componente2.CE
  N9: Parte1.D49, Componente2.CSN
  N10: Parte1.D50/MISO, Componente2.MISO
  N11: Parte1.D51/MOSI, Componente2.MOSI
  N12: Parte1.D52/SCK, Componente2.SCK
  N13: U1.VO, R35.wiper
