# Fritzing sketch Esquematico_Transmisor_nrf24l01 (saved by Fritzing 0.9.3b)
breadboards: 1

parts:
  Parte1 = Arduino Mega ADK (Rev3)
  U1 = LCD-16X2 [package=lcd-16x2]
  R35 = Rotary Potentiometer (Large) [maximum_resistance=10kΩ package=THT]
  Componente2 = nRF24L01+

nets:
  5V: Parte1.5V, U1.VDD, U1.A, R35.leg2, Componente2.VCC
  GND: Parte1.GND, U1.VSS, U1.R_W, U1.K, R35.leg1, Componente2.GND
  N1: Parte1.D48, U1.DB7
  N2: Parte1.D49, U1.DB5
  N3: Parte1.D50/MISO, U1.DB6
  N4: Parte1.D51/MOSI, U1.DB4
  N5: Parte1.D52/SCK, U1.E
  N6: Parte1.D53/SS, U1.RS
  N7: U1.VO, R35.wiper
